// Digital circuit CPU.dig as structural Verilog
module CPU (
  input  clk,
  input  CLR_PC
);

  wire comparator_1_eq, comparator_2_eq, comparator_3_eq, comparator_4_eq, comparator_5_eq, comparator_6_eq,
       comparator_7_eq, comparator_8_eq, comparator_9_eq;
  wire [7:0] alu_1_q, rom_1_d;
  wire [15:0] programme_counter_1_ln, rom_3_d;

  Comparator #(.Bits(8)) comparator_1 (.a(rom_1_d), .b(8'h1), .eq(comparator_1_eq));  // open: gt, lt
  Comparator #(.Bits(8)) comparator_2 (.a(rom_1_d), .b(8'h2), .eq(comparator_2_eq));  // open: gt, lt
  Comparator #(.Bits(8)) comparator_3 (.a(rom_1_d), .b(8'h1), .eq(comparator_3_eq));  // open: gt, lt
  Comparator #(.Bits(8)) comparator_4 (.a(rom_1_d), .b(8'h1), .eq(comparator_4_eq));  // open: gt, lt
  Comparator #(.Bits(8)) comparator_5 (.a(rom_1_d), .b(8'h1), .eq(comparator_5_eq));  // open: gt, lt
  Comparator #(.Bits(8)) comparator_6 (.a(rom_1_d), .b(8'h1), .eq(comparator_6_eq));  // open: gt, lt
  Comparator #(.Bits(8)) comparator_7 (.a(rom_1_d), .b(8'h1), .eq(comparator_7_eq));  // open: gt, lt
  Comparator #(.Bits(8)) comparator_8 (.a(rom_1_d), .b(8'h1), .eq(comparator_8_eq));  // open: gt, lt
  Comparator #(.Bits(8)) comparator_9 (.a(rom_1_d), .b(8'h1), .eq(comparator_9_eq));  // open: gt, lt
  Programme_Counter programme_counter_1 (
    .DAT(alu_1_q), .ADR(rom_3_d), .CLK(clk), .JMP(comparator_1_eq), .CJP(comparator_2_eq), .CLR(CLR_PC),
    .LN(programme_counter_1_ln));
  ALU alu_1 (.CMD(rom_1_d), .DAT(alu_1_q), .CLK(clk), .Q(alu_1_q));
  ROM #(.AddrBits(16), .Bits(8)) rom_1 (.A(programme_counter_1_ln), .sel(1'b1), .D(rom_1_d));
  ROM #(.AddrBits(16), .Bits(8)) rom_2 (.A(programme_counter_1_ln), .sel(1'b1), .D(alu_1_q));
  ROM #(.AddrBits(16), .Bits(16)) rom_3 (.A(programme_counter_1_ln), .sel(1'b1), .D(rom_3_d));
  // RAM ram_1: pin names not known; wires that end beside it: alu_1_q, rom_3_d, comparator_3_eq, comparator_4_eq, comparator_5_eq, comparator_6_eq, comparator_7_eq, comparator_8_eq, comparator_9_eq, clk, alu_1_q, rom_3_d

  // Notes on the sheet:
  //   clk: Hz: 10
  //   LN
  //   CMD
  //   DAT
  //   ADR
  //   CLK
  //   LN: output from the programmme counter,
  //   the current line of code being executed
  //   - Flash memory
endmodule
